# Fritzing sketch Maquette (saved by Fritzing 0.9.3b)
breadboards: 2

parts:
  LED5 = smd LED [color="Yellow (595nm)" package="0805 [SMD]"]
  Raspberry_Pi_2 = Raspberry Pi 3 [part_number=RPI-3-V1.2]
  LED3 = smd LED [color="Green (555nm)" package="0805 [SMD]"]
  R1 = Resistor [tolerance=±5% resistance=3.3k package=THT]
  S1 = Toggle Switch [package=THT]
  R9 = Resistor [tolerance=±5% resistance=1k package=THT]
  hc-sr1 = hc-sr04
  R10 = Resistor [tolerance=±5% resistance=1k package=THT]
  Composant1 = Arduino Uno (Rev3)
  LED4 = smd LED [color="Red (633nm)" package="0805 [SMD]"]
  R14 = Resistor [tolerance=±5% resistance=1k package=THT]
  R12 = Resistor [tolerance=±5% resistance=2.2k package=THT]
  R11 = Resistor [tolerance=±5% resistance=1k package=THT]
  R4 = Resistor [tolerance=±5% resistance=1k package=THT]
  hc-sr2 = hc-sr04
  Raspberry_Pi_1 = Raspberry Pi 3 [part_number=RPI-3-V1.2]
  R13 = Resistor [tolerance=±5% resistance=3.3k package=THT]
  LED1 = smd LED [color="Red (633nm)" package="0805 [SMD]"]
  R7 = Resistor [tolerance=±5% resistance=1k package=THT]
  LED2 = smd LED [color="Green (555nm)" package="0805 [SMD]"]
  R5 = Resistor [tolerance=±5% resistance=2.2k package=THT]
  J1 = male pin header, 4 pins [form="♂ (male)"]
  J2 = male pin header, 4 pins [form="♂ (male)"]
  Composant3 = TXB0108 8-channel Bi-directional Logic Level Converter

nets:
  N1: LED5.cathode, Composant1.D4
  N2: LED5.anode, R9.Pin_0
  N3: Raspberry_Pi_2.GPIO2, hc-sr2.Trig, J1.pin2
  N4: Raspberry_Pi_2.GPIO3, Raspberry_Pi_2.GPIO4, R1.Pin_1, R5.Pin_0
  N5: Raspberry_Pi_2.GPIO17, Composant3.B8
  N6: Raspberry_Pi_2.GPIO27, Composant3.B7
  N7: Raspberry_Pi_2.GPIO22, Raspberry_Pi_2.3V3, Composant3.B6
  GND: Raspberry_Pi_2.GPIO14, Raspberry_Pi_2.GND, LED3.anode, R1.Pin_0, R9.Pin_1, hc-sr1.GND, Composant1.GND, LED4.anode, R14.Pin_1, hc-sr2.GND, Raspberry_Pi_1.GND, R13.Pin_0, LED1.anode, LED2.anode, J1.pin4, J2.pin2, Composant3.GND
  N8: LED3.cathode, R10.Pin_1
  N9: S1.COM, Composant1.D5_PWM, R14.Pin_0
  VCC: S1.L2, hc-sr1.VCC, Composant1.5V, hc-sr2.VCC, J1.pin3, J2.pin1, Composant3.VCCA
  N10: hc-sr1.Trig, Raspberry_Pi_1.GPIO2, J2.pin3
  N11: hc-sr1.Echo, R12.Pin_0, J2.pin4
  N12: R10.Pin_0, Composant1.D7
  N13: Composant1.D8, Composant3.A8
  N14: Composant1.D9_PWM, Composant3.A7
  N15: Composant1.D10_PWM/SS, Composant3.A6
  N16: Composant1.D11_PWM/MOSI, Composant3.A5
  N17: Composant1.D12/MISO, Composant3.A4
  N18: Composant1.D13/SCK, Composant3.A3
  N19: Composant1.D2, R11.Pin_0
  N20: Composant1.D3_PWM, R4.Pin_0
  N21: Composant1.D6_PWM, R7.Pin_0
  N22: Composant1.3V3, Composant3.VCCB
  N23: LED4.cathode, R7.Pin_1
  N24: R12.Pin_1, Raspberry_Pi_1.GPIO3, R13.Pin_1
  N25: R11.Pin_1, LED1.cathode
  N26: R4.Pin_1, LED2.cathode
  N27: hc-sr2.Echo, R5.Pin_1, J1.pin1
  N28: Raspberry_Pi_1.GPIO17, Composant3.B5
  N29: Raspberry_Pi_1.GPIO27, Composant3.B4
  N30: Raspberry_Pi_1.GPIO22, Composant3.B3

notes:
  Watchdog I/O
  Ultrasonic Sensor
  U.S. Trigger
  Echo 3.3V
  Actual RPi State
  Alive
  RPi State Order

custom parts:
  TXB0108 8-channel Bi-directional Logic Level Converter: Because the Arduino (and Basic Stamp) are 5V devices, and most modern sensors, displays, flash cards and modes are 3.3V-only, many makers find that they need to perform level shifting/conversion to protect the 3.3V device from 5V. Although one can use resistors to make a divider, for high speed transfers, the resistors can add a lot of slew and cause havoc that is tough to debug. For that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
